# Fritzing sketch dispositivo - ckt esquematico (saved by Fritzing 0.9.2b)
breadboards: 1

parts:
  U1 = NodeMCU V1.0
  DHT1 = DHT22 Humidity and Temperature Sensor  # not connected
  R1 = Resistor [tolerance=±5% resistance=10k package="0603 [SMD]"]

nets:
  N1: U1.D1, R1.Pin_1
  N2: U1.3V3, R1.Pin_0

notes:
  Fonte micro-USB 5V/2A ---->

custom parts:
  NodeMCU V1.0: ESP8266 based NodeMCU
